// Logisim project FinalProject.circ as structural Verilog
module _16_bit_ALU (
  input  [15:0] A,
  input  [15:0] B,
  input  [1:0] ALU_Op,
  output [15:0] ALU_Out,
  output Zero
);

  wire and_1_out;
  wire [15:0] adder_1_out, and_2_out, multiplexer_1_out, not_1_out, not_2_out, or_1_out;

  Multiplexer #(.width(16), .enable("false")) multiplexer_1 (
    .in0(B), .in1(not_1_out), .out(multiplexer_1_out), .sel(and_1_out));
  assign not_1_out = ~B;  // NOT_Gate not_1, 16 bits wide
  and and_1 (and_1_out, ALU_Op[0], ALU_Op[1]);
  Adder #(.width(16)) adder_1 (.a(A), .b(multiplexer_1_out), .out(adder_1_out), .cin(and_1_out));  // open: cout
  assign and_2_out = multiplexer_1_out & A;  // AND_Gate and_2, 16 bits wide
  assign or_1_out = multiplexer_1_out | A;  // OR_Gate or_1, 16 bits wide
  Multiplexer #(.select(2), .width(16), .enable("false")) multiplexer_2 (
    .in0(adder_1_out), .in1(and_2_out), .in2(or_1_out), .in3(adder_1_out), .out(ALU_Out), .sel(ALU_Op));
  assign not_2_out = ~ALU_Out;  // NOT_Gate not_2, 16 bits wide
  and and_3 (Zero, not_2_out[0], not_2_out[1], not_2_out[2], not_2_out[3], not_2_out[4], not_2_out[5], not_2_out[6], not_2_out[7], not_2_out[8], not_2_out[9], not_2_out[10], not_2_out[11], not_2_out[12], not_2_out[13], not_2_out[14], not_2_out[15]);

  // Notes on the sheet:
  //   16 Bit ALU
  //   00 = ADD
  //   01 = AND
  //   10 = OR
  //   11 = SUB
  //   sub not B
  //   sub cin
  //   sub
endmodule

module _8x4_bit_Register_File (
  input  [15:0] Data_In,
  input  [2:0] Read_Addr_1,
  input  Write_Enable,
  input  [2:0] Write_Addr,
  input  [2:0] Read_Addr_2,
  input  Clock,
  output [15:0] Read_1_Data,
  output [15:0] Read_2_Data
);

  wire demultiplexer_1_out0, demultiplexer_1_out1, demultiplexer_1_out2, demultiplexer_1_out3,
       demultiplexer_1_out4, demultiplexer_1_out5, demultiplexer_1_out6, demultiplexer_1_out7;
  wire [15:0] register_1_q, register_2_q, register_3_q, register_4_q, register_5_q, register_6_q,
       register_7_q, register_8_q;

  Demultiplexer #(.select(3), .enable("false")) demultiplexer_1 (
    .out0(demultiplexer_1_out0), .out1(demultiplexer_1_out1), .out2(demultiplexer_1_out2),
    .out3(demultiplexer_1_out3), .out4(demultiplexer_1_out4), .out5(demultiplexer_1_out5),
    .out6(demultiplexer_1_out6), .out7(demultiplexer_1_out7), .in(Write_Enable), .sel(Write_Addr));
  Register #(.width(16)) register_1 (
    .D(Data_In), .en(demultiplexer_1_out0), .Q(register_1_q), .clk(Clock));  // open: clr
  Register #(.width(16)) register_2 (
    .D(Data_In), .en(demultiplexer_1_out1), .Q(register_2_q), .clk(Clock));  // open: clr
  Register #(.width(16)) register_3 (
    .D(Data_In), .en(demultiplexer_1_out2), .Q(register_3_q), .clk(Clock));  // open: clr
  Register #(.width(16)) register_4 (
    .D(Data_In), .en(demultiplexer_1_out3), .Q(register_4_q), .clk(Clock));  // open: clr
  Register #(.width(16)) register_5 (
    .D(Data_In), .en(demultiplexer_1_out4), .Q(register_5_q), .clk(Clock));  // open: clr
  Register #(.width(16)) register_6 (
    .D(Data_In), .en(demultiplexer_1_out5), .Q(register_6_q), .clk(Clock));  // open: clr
  Register #(.width(16)) register_7 (
    .D(Data_In), .en(demultiplexer_1_out6), .Q(register_7_q), .clk(Clock));  // open: clr
  Register #(.width(16)) register_8 (
    .D(Data_In), .en(demultiplexer_1_out7), .Q(register_8_q), .clk(Clock));  // open: clr
  Multiplexer #(.select(3), .width(16), .enable("false")) multiplexer_1 (
    .in0(register_1_q), .in1(register_2_q), .in2(register_3_q), .in3(register_4_q), .in4(register_5_q),
    .in5(register_6_q), .in6(register_7_q), .in7(register_8_q), .out(Read_1_Data), .sel(Read_Addr_1));
  Multiplexer #(.select(3), .width(16), .enable("false")) multiplexer_2 (
    .in0(register_1_q), .in1(register_2_q), .in2(register_3_q), .in3(register_4_q), .in4(register_5_q),
    .in5(register_6_q), .in6(register_7_q), .in7(register_8_q), .out(Read_2_Data), .sel(Read_Addr_2));

  // Notes on the sheet:
  //   8x16-bit Register File
endmodule

module Basic_16_Bit_CPU (
  input  clock,
  output [15:0] CPU_Op_Out
);

  wire control_logic_1_default_alu, control_logic_1_imm_sel, control_logic_1_lw, control_logic_1_mem_write,
       control_logic_1_reg_write, control_logic_1_sw;
  wire [1:0] control_logic_1_alu_op, multiplexer_4_out;
  wire [2:0] control_logic_1_src1, control_logic_1_wa, multiplexer_1_out;
  wire [5:0] adder_1_out, PC_q;
  wire [15:0] control_logic_1_src2, multiplexer_2_out, multiplexer_3_out,
       n8x4_bit_register_file_1_read_1_data, n8x4_bit_register_file_1_read_2_data, ram_2_data;
  wire [26:0] ram_1_data;

  Adder #(.width(6)) adder_1 (.a(PC_q), .b(6'b000001), .out(adder_1_out));  // open: cin, cout
  Register #(.width(6)) PC (.D(adder_1_out), .Q(PC_q), .clk(clock));  // open: en, clr
  RAM #(.addrWidth(6), .dataWidth(27)) ram_1 (.addr(PC_q), .data(ram_1_data), .clk(clock));  // open: sel, ld, clr
  Control_Logic control_logic_1 (
    .in_1(ram_1_data), .WA(control_logic_1_wa), .SRC1(control_logic_1_src1), .SRC2(control_logic_1_src2),
    .imm_sel(control_logic_1_imm_sel), .SW(control_logic_1_sw), .LW(control_logic_1_lw),
    .ALU_OP(control_logic_1_alu_op), .default_alu(control_logic_1_default_alu),
    .Reg_Write(control_logic_1_reg_write), .Mem_Write(control_logic_1_mem_write));  // open: BEQ, jump, SLT, SGT
  Multiplexer #(.width(3), .enable("false")) multiplexer_1 (
    .in0(control_logic_1_src2[15:13]), .in1(control_logic_1_wa), .out(multiplexer_1_out),
    .sel(control_logic_1_sw));
  _8x4_bit_Register_File u_8x4_bit_register_file_1 (
    .Data_In(multiplexer_2_out), .Write_Enable(control_logic_1_reg_write), .Clock(clock),
    .Write_Addr(control_logic_1_wa), .Read_Addr_1(control_logic_1_src1), .Read_Addr_2(multiplexer_1_out),
    .Read_1_Data(n8x4_bit_register_file_1_read_1_data), .Read_2_Data(n8x4_bit_register_file_1_read_2_data));
  Multiplexer #(.width(16), .enable("false")) multiplexer_2 (
    .in0(CPU_Op_Out), .in1(ram_2_data), .out(multiplexer_2_out), .sel(control_logic_1_lw));
  _16_bit_ALU u_16_bit_alu_1 (
    .A(n8x4_bit_register_file_1_read_1_data), .B(multiplexer_3_out), .ALU_Op(multiplexer_4_out),
    .ALU_Out(CPU_Op_Out));  // open: Zero
  Multiplexer #(.width(16), .enable("false")) multiplexer_3 (
    .in0(n8x4_bit_register_file_1_read_2_data), .in1(control_logic_1_src2), .out(multiplexer_3_out),
    .sel(control_logic_1_imm_sel));
  Multiplexer #(.width(2), .enable("false")) multiplexer_4 (
    .in0(control_logic_1_alu_op), .in1(2'b00), .out(multiplexer_4_out), .sel(control_logic_1_default_alu));
  RAM #(.addrWidth(16), .dataWidth(16), .bus("separate")) ram_2 (
    .addr(CPU_Op_Out), .din(n8x4_bit_register_file_1_read_2_data), .data(ram_2_data),
    .str(control_logic_1_mem_write), .clk(clock));  // open: sel, ld, clr

  // Notes on the sheet:
  //   ALU op
  //   src2
  //   immed data
  //   immed select
  //   SW
  //   LW
  //   src1
endmodule

module Control_Logic (
  input  [26:0] in_1,
  output [2:0] WA,
  output [2:0] SRC1,
  output [15:0] SRC2,
  output imm_sel,
  output SW,
  output LW,
  output BEQ,
  output jump,
  output SLT,
  output SGT,
  output [1:0] ALU_OP,
  output default_alu,
  output Reg_Write,
  output Mem_Write
);

  wire not_1_out, not_2_out, not_3_out, not_4_out, not_5_out, not_6_out, not_7_out, not_8_out, not_9_out,
       not_10_out, not_11_out, not_12_out, not_13_out, or_2_out;

  not not_1 (not_1_out, in_1[24]);
  not not_2 (not_2_out, in_1[23]);
  not not_3 (not_3_out, in_1[22]);
  not not_4 (not_4_out, in_1[25]);
  not not_5 (not_5_out, in_1[23]);
  not not_6 (not_6_out, in_1[22]);
  not not_7 (not_7_out, in_1[26]);
  not not_8 (not_8_out, in_1[26]);
  not not_9 (not_9_out, in_1[22]);
  not not_10 (not_10_out, in_1[26]);
  not not_11 (not_11_out, in_1[24]);
  not not_12 (not_12_out, in_1[26]);
  not not_13 (not_13_out, in_1[25]);
  and and_1 (Mem_Write, in_1[26], in_1[25], not_1_out, not_2_out, not_3_out);
  and and_2 (LW, in_1[26], not_4_out, in_1[24], not_5_out, not_6_out);
  and and_3 (BEQ, not_7_out, in_1[25], in_1[24], in_1[23], in_1[22]);
  and and_4 (jump, not_8_out, in_1[25], in_1[24], in_1[23], not_9_out);
  and and_5 (SLT, not_10_out, in_1[25], not_11_out, in_1[23], in_1[22]);
  and and_6 (SGT, not_12_out, not_13_out, in_1[24], in_1[23], in_1[22]);
  or or_1 (default_alu, jump, LW, Mem_Write);
  or or_2 (or_2_out, jump, BEQ, Mem_Write);
  not not_14 (Reg_Write, or_2_out);

  assign ALU_OP = in_1[23:22];
  assign imm_sel = in_1[26];
  assign SRC1 = in_1[18:16];
  assign SRC2 = in_1[15:0];
  assign SW = Mem_Write;
  assign WA = in_1[21:19];

  // Notes on the sheet:
  //   OP
  //   WA/RA2
  //   RA1
  //   OFF/RA2
  //   sw
  //   lw
  //   beq
  //   jump
  //   slt
  //   sgt
endmodule

module CPU_w__beq (
  input  clock,
  output [15:0] CPU_Op_Out
);

  wire and_1_out, control_logic_1_beq, control_logic_1_default_alu, control_logic_1_imm_sel,
       control_logic_1_lw, control_logic_1_mem_write, control_logic_1_reg_write, control_logic_1_sw,
       n16_bit_alu_1_zero;
  wire [1:0] control_logic_1_alu_op, multiplexer_5_out;
  wire [2:0] control_logic_1_src1, control_logic_1_wa, multiplexer_2_out;
  wire [15:0] adder_1_out, adder_2_out, adder_3_out, control_logic_1_src2, multiplexer_1_out,
       multiplexer_3_out, multiplexer_4_out, n8x4_bit_register_file_1_read_1_data,
       n8x4_bit_register_file_1_read_2_data, PC_q, ram_2_data;
  wire [26:0] ram_1_data;

  Multiplexer #(.width(16), .enable("false")) multiplexer_1 (
    .in0(adder_2_out), .in1(adder_1_out), .out(multiplexer_1_out), .sel(and_1_out));
  Adder #(.width(16)) adder_1 (.a(adder_3_out), .b(16'h1), .out(adder_1_out));  // open: cin, cout
  Adder #(.width(16)) adder_2 (.a(PC_q), .b(16'h1), .out(adder_2_out));  // open: cin, cout
  Register #(.width(16)) PC (.D(multiplexer_1_out), .Q(PC_q), .clk(clock));  // open: en, clr
  RAM #(.addrWidth(16), .dataWidth(27)) ram_1 (.addr(PC_q), .data(ram_1_data), .clk(clock));  // open: sel, ld, clr
  Control_Logic control_logic_1 (
    .in_1(ram_1_data), .WA(control_logic_1_wa), .SRC1(control_logic_1_src1), .SRC2(control_logic_1_src2),
    .imm_sel(control_logic_1_imm_sel), .SW(control_logic_1_sw), .LW(control_logic_1_lw),
    .BEQ(control_logic_1_beq), .ALU_OP(control_logic_1_alu_op), .default_alu(control_logic_1_default_alu),
    .Reg_Write(control_logic_1_reg_write), .Mem_Write(control_logic_1_mem_write));  // open: jump, SLT, SGT
  and and_1 (and_1_out, control_logic_1_beq, n16_bit_alu_1_zero);
  Multiplexer #(.width(3), .enable("false")) multiplexer_2 (
    .in0(control_logic_1_src2[15:13]), .in1(control_logic_1_wa), .out(multiplexer_2_out),
    .sel(control_logic_1_sw));
  Adder #(.width(16)) adder_3 (.a(control_logic_1_src2), .b(adder_2_out), .out(adder_3_out));  // open: cin, cout
  _8x4_bit_Register_File u_8x4_bit_register_file_1 (
    .Data_In(multiplexer_3_out), .Write_Enable(control_logic_1_reg_write), .Clock(clock),
    .Write_Addr(control_logic_1_wa), .Read_Addr_1(control_logic_1_src1), .Read_Addr_2(multiplexer_2_out),
    .Read_1_Data(n8x4_bit_register_file_1_read_1_data), .Read_2_Data(n8x4_bit_register_file_1_read_2_data));
  Multiplexer #(.width(16), .enable("false")) multiplexer_3 (
    .in0(CPU_Op_Out), .in1(ram_2_data), .out(multiplexer_3_out), .sel(control_logic_1_lw));
  _16_bit_ALU u_16_bit_alu_1 (
    .A(n8x4_bit_register_file_1_read_1_data), .B(multiplexer_4_out), .ALU_Op(multiplexer_5_out),
    .ALU_Out(CPU_Op_Out), .Zero(n16_bit_alu_1_zero));
  Multiplexer #(.width(16), .enable("false")) multiplexer_4 (
    .in0(n8x4_bit_register_file_1_read_2_data), .in1(control_logic_1_src2), .out(multiplexer_4_out),
    .sel(control_logic_1_imm_sel));
  Multiplexer #(.width(2), .enable("false")) multiplexer_5 (
    .in0(control_logic_1_alu_op), .in1(2'b00), .out(multiplexer_5_out), .sel(control_logic_1_default_alu));
  RAM #(.addrWidth(16), .dataWidth(16), .bus("separate")) ram_2 (
    .addr(CPU_Op_Out), .din(n8x4_bit_register_file_1_read_2_data), .data(ram_2_data),
    .str(control_logic_1_mem_write), .clk(clock));  // open: sel, ld, clr

  // Notes on the sheet:
  //   ALU op
  //   src2
  //   immed data
  //   immed select
  //   SW
  //   LW
  //   src1
endmodule

module CPU_w__beq__j (
  input  clock,
  output [15:0] CPU_Op_Out
);

  wire and_1_out, control_logic_1_beq, control_logic_1_default_alu, control_logic_1_imm_sel,
       control_logic_1_jump, control_logic_1_lw, control_logic_1_mem_write, control_logic_1_reg_write,
       control_logic_1_sw, n16_bit_alu_1_zero;
  wire [1:0] control_logic_1_alu_op, multiplexer_6_out;
  wire [2:0] control_logic_1_src1, control_logic_1_wa, multiplexer_3_out;
  wire [15:0] adder_1_out, adder_2_out, adder_3_out, control_logic_1_src2, multiplexer_1_out,
       multiplexer_2_out, multiplexer_4_out, multiplexer_5_out, n8x4_bit_register_file_1_read_1_data,
       n8x4_bit_register_file_1_read_2_data, PC_q, ram_2_data;
  wire [26:0] ram_1_data;

  Multiplexer #(.width(16), .enable("false")) multiplexer_1 (
    .in0(adder_2_out), .in1(adder_1_out), .out(multiplexer_1_out), .sel(and_1_out));
  Adder #(.width(16)) adder_1 (.a(adder_3_out), .b(16'h1), .out(adder_1_out));  // open: cin, cout
  Adder #(.width(16)) adder_2 (.a(PC_q), .b(16'h1), .out(adder_2_out));  // open: cin, cout
  Multiplexer #(.width(16), .enable("false")) multiplexer_2 (
    .in0(multiplexer_1_out), .in1(adder_3_out), .out(multiplexer_2_out), .sel(control_logic_1_jump));
  Register #(.width(16)) PC (.D(multiplexer_2_out), .Q(PC_q), .clk(clock));  // open: en, clr
  RAM #(.addrWidth(16), .dataWidth(27)) ram_1 (.addr(PC_q), .data(ram_1_data), .clk(clock));  // open: sel, ld, clr
  Control_Logic control_logic_1 (
    .in_1(ram_1_data), .WA(control_logic_1_wa), .SRC1(control_logic_1_src1), .SRC2(control_logic_1_src2),
    .imm_sel(control_logic_1_imm_sel), .SW(control_logic_1_sw), .LW(control_logic_1_lw),
    .BEQ(control_logic_1_beq), .jump(control_logic_1_jump), .ALU_OP(control_logic_1_alu_op),
    .default_alu(control_logic_1_default_alu), .Reg_Write(control_logic_1_reg_write),
    .Mem_Write(control_logic_1_mem_write));  // open: SLT, SGT
  and and_1 (and_1_out, control_logic_1_beq, n16_bit_alu_1_zero);
  Multiplexer #(.width(3), .enable("false")) multiplexer_3 (
    .in0(control_logic_1_src2[15:13]), .in1(control_logic_1_wa), .out(multiplexer_3_out),
    .sel(control_logic_1_sw));
  Adder #(.width(16)) adder_3 (.a(control_logic_1_src2), .b(adder_2_out), .out(adder_3_out));  // open: cin, cout
  _8x4_bit_Register_File u_8x4_bit_register_file_1 (
    .Data_In(multiplexer_4_out), .Write_Enable(control_logic_1_reg_write), .Clock(clock),
    .Write_Addr(control_logic_1_wa), .Read_Addr_1(control_logic_1_src1), .Read_Addr_2(multiplexer_3_out),
    .Read_1_Data(n8x4_bit_register_file_1_read_1_data), .Read_2_Data(n8x4_bit_register_file_1_read_2_data));
  Multiplexer #(.width(16), .enable("false")) multiplexer_4 (
    .in0(CPU_Op_Out), .in1(ram_2_data), .out(multiplexer_4_out), .sel(control_logic_1_lw));
  _16_bit_ALU u_16_bit_alu_1 (
    .A(n8x4_bit_register_file_1_read_1_data), .B(multiplexer_5_out), .ALU_Op(multiplexer_6_out),
    .ALU_Out(CPU_Op_Out), .Zero(n16_bit_alu_1_zero));
  Multiplexer #(.width(16), .enable("false")) multiplexer_5 (
    .in0(n8x4_bit_register_file_1_read_2_data), .in1(control_logic_1_src2), .out(multiplexer_5_out),
    .sel(control_logic_1_imm_sel));
  Multiplexer #(.width(2), .enable("false")) multiplexer_6 (
    .in0(control_logic_1_alu_op), .in1(2'b00), .out(multiplexer_6_out), .sel(control_logic_1_default_alu));
  RAM #(.addrWidth(16), .dataWidth(16), .bus("separate")) ram_2 (
    .addr(CPU_Op_Out), .din(n8x4_bit_register_file_1_read_2_data), .data(ram_2_data),
    .str(control_logic_1_mem_write), .clk(clock));  // open: sel, ld, clr

  // Notes on the sheet:
  //   ALU op
  //   src2
  //   immed data
  //   immed select
  //   SW
  //   LW
  //   src1
endmodule

module CPU_w__beq__j__slt__sgt (
  input  clock,
  output [15:0] CPU_Op_Out
);

  wire and_1_out, and_2_out, control_logic_1_beq, control_logic_1_default_alu, control_logic_1_imm_sel,
       control_logic_1_jump, control_logic_1_lw, control_logic_1_mem_write, control_logic_1_reg_write,
       control_logic_1_sgt, control_logic_1_slt, control_logic_1_sw, n16_bit_alu_1_zero, not_1_out, not_2_out;
  wire [1:0] control_logic_1_alu_op, multiplexer_8_out;
  wire [2:0] control_logic_1_src1, control_logic_1_wa, multiplexer_3_out;
  wire [15:0] adder_1_out, adder_2_out, adder_3_out, bit_extender_1_out, bit_extender_2_out,
       control_logic_1_src2, multiplexer_1_out, multiplexer_2_out, multiplexer_4_out, multiplexer_5_out,
       multiplexer_6_out, multiplexer_7_out, n8x4_bit_register_file_1_read_1_data,
       n8x4_bit_register_file_1_read_2_data, PC_q, ram_2_data;
  wire [26:0] ram_1_data;

  Multiplexer #(.width(16), .enable("false")) multiplexer_1 (
    .in0(adder_2_out), .in1(adder_1_out), .out(multiplexer_1_out), .sel(and_1_out));
  Adder #(.width(16)) adder_1 (.a(adder_3_out), .b(16'h1), .out(adder_1_out));  // open: cin, cout
  Adder #(.width(16)) adder_2 (.a(PC_q), .b(16'h1), .out(adder_2_out));  // open: cin, cout
  Register #(.width(16)) PC (.D(multiplexer_2_out), .Q(PC_q), .clk(clock));  // open: en, clr
  Multiplexer #(.width(16), .enable("false")) multiplexer_2 (
    .in0(multiplexer_1_out), .in1(adder_3_out), .out(multiplexer_2_out), .sel(control_logic_1_jump));
  RAM #(.addrWidth(16), .dataWidth(27)) ram_1 (.addr(PC_q), .data(ram_1_data), .clk(clock));  // open: sel, ld, clr
  Control_Logic control_logic_1 (
    .in_1(ram_1_data), .WA(control_logic_1_wa), .SRC1(control_logic_1_src1), .SRC2(control_logic_1_src2),
    .imm_sel(control_logic_1_imm_sel), .SW(control_logic_1_sw), .LW(control_logic_1_lw),
    .BEQ(control_logic_1_beq), .jump(control_logic_1_jump), .SLT(control_logic_1_slt),
    .SGT(control_logic_1_sgt), .ALU_OP(control_logic_1_alu_op), .default_alu(control_logic_1_default_alu),
    .Reg_Write(control_logic_1_reg_write), .Mem_Write(control_logic_1_mem_write));
  and and_1 (and_1_out, control_logic_1_beq, n16_bit_alu_1_zero);
  Multiplexer #(.width(3), .enable("false")) multiplexer_3 (
    .in0(control_logic_1_src2[15:13]), .in1(control_logic_1_wa), .out(multiplexer_3_out),
    .sel(control_logic_1_sw));
  Adder #(.width(16)) adder_3 (.a(control_logic_1_src2), .b(adder_2_out), .out(adder_3_out));  // open: cin, cout
  Multiplexer #(.width(16), .enable("false")) multiplexer_4 (
    .in0(multiplexer_5_out), .in1(bit_extender_1_out), .out(multiplexer_4_out), .sel(control_logic_1_sgt));
  and and_2 (and_2_out, not_2_out, not_1_out);
  not not_1 (not_1_out, n16_bit_alu_1_zero);
  Multiplexer #(.width(16), .enable("false")) multiplexer_5 (
    .in0(multiplexer_6_out), .in1(bit_extender_2_out), .out(multiplexer_5_out), .sel(control_logic_1_slt));
  not not_2 (not_2_out, CPU_Op_Out[15]);
  _8x4_bit_Register_File u_8x4_bit_register_file_1 (
    .Data_In(multiplexer_4_out), .Write_Enable(control_logic_1_reg_write), .Clock(clock),
    .Write_Addr(control_logic_1_wa), .Read_Addr_1(control_logic_1_src1), .Read_Addr_2(multiplexer_3_out),
    .Read_1_Data(n8x4_bit_register_file_1_read_1_data), .Read_2_Data(n8x4_bit_register_file_1_read_2_data));
  assign bit_extender_1_out = {{15{1'b0}}, and_2_out};  // Bit_Extender bit_extender_1
  Multiplexer #(.width(16), .enable("false")) multiplexer_6 (
    .in0(CPU_Op_Out), .in1(ram_2_data), .out(multiplexer_6_out), .sel(control_logic_1_lw));
  _16_bit_ALU u_16_bit_alu_1 (
    .A(n8x4_bit_register_file_1_read_1_data), .B(multiplexer_7_out), .ALU_Op(multiplexer_8_out),
    .ALU_Out(CPU_Op_Out), .Zero(n16_bit_alu_1_zero));
  Multiplexer #(.width(16), .enable("false")) multiplexer_7 (
    .in0(n8x4_bit_register_file_1_read_2_data), .in1(control_logic_1_src2), .out(multiplexer_7_out),
    .sel(control_logic_1_imm_sel));
  Multiplexer #(.width(2), .enable("false")) multiplexer_8 (
    .in0(control_logic_1_alu_op), .in1(2'b00), .out(multiplexer_8_out), .sel(control_logic_1_default_alu));
  assign bit_extender_2_out = {{15{1'b0}}, CPU_Op_Out[15]};  // Bit_Extender bit_extender_2
  RAM #(.addrWidth(16), .dataWidth(16), .bus("separate")) ram_2 (
    .addr(CPU_Op_Out), .din(n8x4_bit_register_file_1_read_2_data), .data(ram_2_data),
    .str(control_logic_1_mem_write), .clk(clock));  // open: sel, ld, clr

  // Notes on the sheet:
  //   ALU op
  //   src2
  //   immed data
  //   immed select
  //   SW
  //   LW
  //   src1
endmodule

module Carry_Look_Ahead_Adder (
  input  Cin,
  input  [15:0] A,
  input  [15:0] B,
  output [15:0] Output,
  output Cout
);

  wire n4_bit_cla_block_1_cout, n4_bit_cla_block_2_cout, n4_bit_cla_block_3_cout;

  _4_Bit_CLA_Block u_4_bit_cla_block_1 (
    .A(A[3:0]), .B(B[3:0]), .Cin(Cin), .Cout(n4_bit_cla_block_1_cout), .S0(Output[0]), .S1(Output[1]),
    .S2(Output[2]), .S3(Output[3]));
  _4_Bit_CLA_Block u_4_bit_cla_block_2 (
    .A(A[7:4]), .B(B[7:4]), .Cin(n4_bit_cla_block_1_cout), .Cout(n4_bit_cla_block_2_cout), .S0(Output[4]),
    .S1(Output[5]), .S2(Output[6]), .S3(Output[7]));
  _4_Bit_CLA_Block u_4_bit_cla_block_3 (
    .A(A[11:8]), .B(B[11:8]), .Cin(n4_bit_cla_block_2_cout), .Cout(n4_bit_cla_block_3_cout), .S0(Output[8]),
    .S1(Output[9]), .S2(Output[10]), .S3(Output[11]));
  _4_Bit_CLA_Block u_4_bit_cla_block_4 (
    .A(A[15:12]), .B(B[15:12]), .Cin(n4_bit_cla_block_3_cout), .Cout(Cout), .S0(Output[12]), .S1(Output[13]),
    .S2(Output[14]), .S3(Output[15]));
endmodule

module _4_Bit_CLA_Block (
  input  Cin,
  input  [3:0] A,
  input  [3:0] B,
  output S0,
  output S1,
  output S2,
  output S3,
  output Cout
);

  wire adder_1_cout, adder_2_cout, adder_3_cout, adder_4_cout, and_1_out, and_2_out, and_3_out, and_4_out,
       and_5_out, and_6_out, and_7_out, and_8_out, and_9_out, or_1_out, or_2_out, or_3_out, or_4_out,
       or_5_out, or_6_out, or_7_out;

  Adder #(.width(1)) adder_1 (.a(A[0]), .b(B[0]), .out(S0), .cin(Cin), .cout(adder_1_cout));
  Adder #(.width(1)) adder_2 (.a(A[1]), .b(B[1]), .out(S1), .cin(adder_1_cout), .cout(adder_2_cout));
  Adder #(.width(1)) adder_3 (.a(A[2]), .b(B[2]), .out(S2), .cin(adder_2_cout), .cout(adder_3_cout));
  Adder #(.width(1)) adder_4 (.a(A[3]), .b(B[3]), .out(S3), .cin(adder_3_cout), .cout(adder_4_cout));
  or or_1 (or_1_out, A[0], B[0]);
  and and_1 (and_1_out, A[0], B[0]);
  or or_2 (or_2_out, A[1], B[1]);
  and and_2 (and_2_out, A[1], B[1]);
  or or_3 (or_3_out, A[2], B[2]);
  and and_3 (and_3_out, A[2], B[2]);
  or or_4 (or_4_out, A[3], B[3]);
  and and_4 (and_4_out, A[3], B[3]);
  and and_5 (and_5_out, and_1_out, or_2_out);
  and and_6 (and_6_out, or_4_out, or_3_out, or_2_out, or_1_out);
  or or_5 (or_5_out, and_5_out, and_2_out);
  and and_7 (and_7_out, Cin, and_6_out);
  and and_8 (and_8_out, or_5_out, or_3_out);
  or or_6 (or_6_out, and_8_out, and_3_out);
  and and_9 (and_9_out, or_6_out, or_4_out);
  or or_7 (or_7_out, and_9_out, and_4_out);
  or or_8 (Cout, or_7_out, and_7_out);

  // Notes on the sheet:
  //   p0
  //   g0
  //   p1
  //   g1
  //   p2
  //   g2
  //   p3
  //   g3
endmodule

module Kitchen_Sink_CPU (
  input  clock,
  output [15:0] CPU_Op_Out
);

  wire and_1_out, and_2_out, control_logic_1_beq, control_logic_1_default_alu, control_logic_1_imm_sel,
       control_logic_1_jump, control_logic_1_lw, control_logic_1_mem_write, control_logic_1_reg_write,
       control_logic_1_sgt, control_logic_1_slt, control_logic_1_sw, n16_bit_alu_w_cla_1_zero, not_1_out,
       not_2_out, or_1_out;
  wire [1:0] control_logic_1_alu_op, multiplexer_9_out;
  wire [2:0] control_logic_1_src1, control_logic_1_wa, multiplexer_4_out;
  wire [14:0] control_logic_1_src2;
  wire [15:0] adder_1_out, adder_2_out, adder_3_out, bit_extender_1_out, bit_extender_2_out,
       multiplexer_1_out, multiplexer_2_out, multiplexer_3_out, multiplexer_5_out, multiplexer_6_out,
       multiplexer_7_out, multiplexer_8_out, n8x4_bit_register_file_1_read_1_data,
       n8x4_bit_register_file_1_read_2_data, PC_q, ram_2_data;
  wire [15:15] control_logic_1_src2_2;
  wire [26:0] ram_1_data;

  Multiplexer #(.width(16), .enable("false")) multiplexer_1 (
    .in0(adder_2_out), .in1(adder_1_out), .out(multiplexer_1_out), .sel(and_1_out));
  Adder #(.width(16)) adder_1 (.a(adder_3_out), .b(multiplexer_3_out), .out(adder_1_out));  // open: cin, cout
  Adder #(.width(16)) adder_2 (.a(PC_q), .b(16'h1), .out(adder_2_out));  // open: cin, cout
  Register #(.width(16)) PC (.D(multiplexer_2_out), .Q(PC_q), .clk(clock));  // open: en, clr
  Multiplexer #(.width(16), .enable("false")) multiplexer_2 (
    .in0(multiplexer_1_out), .in1(adder_3_out), .out(multiplexer_2_out), .sel(control_logic_1_jump));
  Multiplexer #(.width(16), .enable("false")) multiplexer_3 (
    .in0(16'h1), .in1({16{1'b1}}), .out(multiplexer_3_out), .sel(control_logic_1_src2_2[15]));
  RAM #(.addrWidth(16), .dataWidth(27)) ram_1 (.addr(PC_q), .data(ram_1_data), .clk(clock));  // open: sel, ld, clr
  Control_Logic control_logic_1 (
    .in_1(ram_1_data), .WA(control_logic_1_wa), .SRC1(control_logic_1_src1),
    .SRC2({control_logic_1_src2_2[15], control_logic_1_src2}), .imm_sel(control_logic_1_imm_sel),
    .SW(control_logic_1_sw), .LW(control_logic_1_lw), .BEQ(control_logic_1_beq), .jump(control_logic_1_jump),
    .SLT(control_logic_1_slt), .SGT(control_logic_1_sgt), .ALU_OP(control_logic_1_alu_op),
    .default_alu(control_logic_1_default_alu), .Reg_Write(control_logic_1_reg_write),
    .Mem_Write(control_logic_1_mem_write));
  and and_1 (and_1_out, control_logic_1_beq, n16_bit_alu_w_cla_1_zero);
  Multiplexer #(.width(3), .enable("false")) multiplexer_4 (
    .in0({control_logic_1_src2_2[15], control_logic_1_src2[14:13]}), .in1(control_logic_1_wa),
    .out(multiplexer_4_out), .sel(or_1_out));
  Adder #(.width(16)) adder_3 (
    .a({control_logic_1_src2_2[15], control_logic_1_src2}), .b(adder_2_out), .out(adder_3_out));  // open: cin, cout
  Multiplexer #(.width(16), .enable("false")) multiplexer_5 (
    .in0(multiplexer_6_out), .in1(bit_extender_1_out), .out(multiplexer_5_out), .sel(control_logic_1_sgt));
  and and_2 (and_2_out, not_2_out, not_1_out);
  not not_1 (not_1_out, n16_bit_alu_w_cla_1_zero);
  Multiplexer #(.width(16), .enable("false")) multiplexer_6 (
    .in0(multiplexer_7_out), .in1(bit_extender_2_out), .out(multiplexer_6_out), .sel(control_logic_1_slt));
  not not_2 (not_2_out, CPU_Op_Out[15]);
  _8x4_bit_Register_File u_8x4_bit_register_file_1 (
    .Data_In(multiplexer_5_out), .Write_Enable(control_logic_1_reg_write), .Clock(clock),
    .Write_Addr(control_logic_1_wa), .Read_Addr_1(control_logic_1_src1), .Read_Addr_2(multiplexer_4_out),
    .Read_1_Data(n8x4_bit_register_file_1_read_1_data), .Read_2_Data(n8x4_bit_register_file_1_read_2_data));
  or or_1 (or_1_out, control_logic_1_sw, control_logic_1_beq);
  assign bit_extender_1_out = {{15{1'b0}}, and_2_out};  // Bit_Extender bit_extender_1
  Multiplexer #(.width(16), .enable("false")) multiplexer_7 (
    .in0(CPU_Op_Out), .in1(ram_2_data), .out(multiplexer_7_out), .sel(control_logic_1_lw));
  _16_bit_ALU_w__CLA u_16_bit_alu_w_cla_1 (
    .A(n8x4_bit_register_file_1_read_1_data), .B(multiplexer_8_out), .ALU_Op(multiplexer_9_out),
    .ALU_Out(CPU_Op_Out), .Zero(n16_bit_alu_w_cla_1_zero));
  Multiplexer #(.width(16), .enable("false")) multiplexer_8 (
    .in0(n8x4_bit_register_file_1_read_2_data), .in1({control_logic_1_src2_2[15], control_logic_1_src2}),
    .out(multiplexer_8_out), .sel(control_logic_1_imm_sel));
  Multiplexer #(.width(2), .enable("false")) multiplexer_9 (
    .in0(control_logic_1_alu_op), .in1(2'b00), .out(multiplexer_9_out), .sel(control_logic_1_default_alu));
  assign bit_extender_2_out = {{15{1'b0}}, CPU_Op_Out[15]};  // Bit_Extender bit_extender_2
  RAM #(.addrWidth(16), .dataWidth(16), .bus("separate")) ram_2 (
    .addr(CPU_Op_Out), .din(n8x4_bit_register_file_1_read_2_data), .data(ram_2_data),
    .str(control_logic_1_mem_write), .clk(clock));  // open: sel, ld, clr

  // Notes on the sheet:
  //   ALU op
  //   src2
  //   immed data
  //   immed select
  //   SW
  //   LW
  //   src1
endmodule

module _16_bit_ALU_w__CLA (
  input  [15:0] A,
  input  [15:0] B,
  input  [1:0] ALU_Op,
  output [15:0] ALU_Out,
  output Zero
);

  wire and_1_out;
  wire [15:0] and_2_out, carry_look_ahead_adder_1_output, multiplexer_1_out, not_1_out, not_2_out, or_1_out;

  Multiplexer #(.width(16), .enable("false")) multiplexer_1 (
    .in0(B), .in1(not_1_out), .out(multiplexer_1_out), .sel(and_1_out));
  assign not_1_out = ~B;  // NOT_Gate not_1, 16 bits wide
  and and_1 (and_1_out, ALU_Op[0], ALU_Op[1]);
  Carry_Look_Ahead_Adder carry_look_ahead_adder_1 (
    .A(A), .B(multiplexer_1_out), .Cin(and_1_out), .Output(carry_look_ahead_adder_1_output));  // open: Cout
  assign and_2_out = multiplexer_1_out & A;  // AND_Gate and_2, 16 bits wide
  assign or_1_out = multiplexer_1_out | A;  // OR_Gate or_1, 16 bits wide
  Multiplexer #(.select(2), .width(16), .enable("false")) multiplexer_2 (
    .in0(carry_look_ahead_adder_1_output), .in1(and_2_out), .in2(or_1_out),
    .in3(carry_look_ahead_adder_1_output), .out(ALU_Out), .sel(ALU_Op));
  assign not_2_out = ~ALU_Out;  // NOT_Gate not_2, 16 bits wide
  and and_3 (Zero, not_2_out[0], not_2_out[1], not_2_out[2], not_2_out[3], not_2_out[4], not_2_out[5], not_2_out[6], not_2_out[7], not_2_out[8], not_2_out[9], not_2_out[10], not_2_out[11], not_2_out[12], not_2_out[13], not_2_out[14], not_2_out[15]);

  // Notes on the sheet:
  //   16 Bit ALU
  //   00 = ADD
  //   01 = AND
  //   10 = OR
  //   11 = SUB
  //   sub not B
  //   sub cin
  //   sub
endmodule
